// Logisim project alu.circ as structural Verilog: 17 circuits, main circuit alu
module alu (
  input  [31:0] A,
  input  [31:0] B,
  input  [3:0] ALUSel,
  output [31:0] Result
);

  wire [31:0] add_out, and_out, cnto_out, div_out, divu_out, mulh_out, mulhu_out, mult_out, or_out, remu_out,
       sir_out, slt_out, sra_out, srl_out, sub_out, xor_out;

  and_0 and_0_1 (.in_1(A), .in_2(B), .out_3(and_out));
  or_1 or_1_1 (.in_1(A), .in_2(B), .out_3(or_out));
  xor_2 xor_2_1 (.in_1(A), .in_2(B), .out_3(xor_out));
  add_3 add_3_1 (.in_1(A), .in_2(B), .out_3(add_out));
  sub_4 sub_4_1 (.in_1(A), .in_2(B), .out_3(sub_out));
  mult_5 mult_5_1 (.in_1(A), .in_2(B), .out_3(mult_out));
  mulhu_6 mulhu_6_1 (.in_1(A), .in_2(B), .out_3(mulhu_out));
  mulh_7 mulh_7_1 (.in_1(A), .in_2(B), .out_3(mulh_out));
  divu_8 divu_8_1 (.in_1(A), .in_2(B), .out_3(divu_out));
  div_9 div_9_1 (.in_1(A), .in_2(B), .out_3(div_out));
  remu_10 remu_10_1 (.in_1(A), .in_2(B), .out_3(remu_out));
  srl_11 srl_11_1 (.in_1(A), .in_2(B), .out_3(srl_out));
  sra_12 sra_12_1 (.in_1(A), .in_2(B), .out_3(sra_out));
  slt_13 slt_13_1 (.A(A), .B(B), .out_3(slt_out));
  sir_14 sir_14_1 (.A(A), .B(B), .out_3(sir_out));
  cnto_15 cnto_15_1 (.in_1(A), .in_2(B), .out_3(cnto_out));
  Multiplexer #(.select(4), .width(32), .enable("false")) multiplexer_1 (
    .in0(and_out), .in1(or_out), .in2(xor_out), .in3(add_out), .in4(sub_out), .in5(mult_out),
    .in6(mulhu_out), .in7(mulh_out), .in8(divu_out), .in9(div_out), .in10(remu_out), .in11(srl_out),
    .in12(sra_out), .in13(slt_out), .in14(sir_out), .in15(cnto_out), .out(Result), .sel(ALUSel));

  // Notes on the sheet:
  //   INPUTS to your circuit
  //   DON'T CHANGE THE LOCATIONS OF THE INPUTS AND OUTPUTS!
  //   OUTPUT from your circuit
endmodule

module and_0 (
  input  [31:0] in_1,
  input  [31:0] in_2,
  output [31:0] out_3
);

  assign out_3 = in_1 & in_2;  // AND_Gate AND_0, 32 bits wide
endmodule

module or_1 (
  input  [31:0] in_1,
  input  [31:0] in_2,
  output [31:0] out_3
);

  assign out_3 = in_1 | in_2;  // OR_Gate OR_1, 32 bits wide
endmodule

module xor_2 (
  input  [31:0] in_1,
  input  [31:0] in_2,
  output [31:0] out_3
);

  assign out_3 = in_1 ^ in_2;  // XOR_Gate xor_1, 32 bits wide
endmodule

module add_3 (
  input  [31:0] in_1,
  input  [31:0] in_2,
  output [31:0] out_3
);

  Adder #(.width(32)) adder_1 (.a(in_1), .b(in_2), .out(out_3));  // open: cin, cout
endmodule

module sub_4 (
  input  [31:0] in_1,
  input  [31:0] in_2,
  output [31:0] out_3
);

  Subtractor #(.width(32)) subtractor_1 (.a(in_1), .b(in_2), .out(out_3));  // open: bin, bout
endmodule

module mult_5 (
  input  [31:0] in_1,
  input  [31:0] in_2,
  output [31:0] out_3
);

  wire xor_1_out;
  wire [30:0] not_2_out, not_4_out, subtractor_1_out, subtractor_2_out;
  wire [31:0] adder_1_out, multiplexer_1_out, multiplexer_2_out, multiplier_1_out, not_5_out;
  wire [31:31] not_1_out, not_3_out;

  Subtractor #(.width(31)) subtractor_1 (.a(in_1[30:0]), .b(31'h1), .out(subtractor_1_out));  // open: bin, bout
  Subtractor #(.width(31)) subtractor_2 (.a(in_2[30:0]), .b(31'h1), .out(subtractor_2_out));  // open: bin, bout
  not not_1 (not_1_out[31], in_1[31]);
  assign not_2_out = ~subtractor_1_out;  // NOT_Gate not_2, 31 bits wide
  not not_3 (not_3_out[31], in_2[31]);
  assign not_4_out = ~subtractor_2_out;  // NOT_Gate not_4, 31 bits wide
  Multiplexer #(.width(32), .enable("false")) multiplexer_1 (
    .in0(in_1), .in1({not_1_out[31], not_2_out}), .out(multiplexer_1_out), .sel(in_1[31]));
  Multiplexer #(.width(32), .enable("false")) multiplexer_2 (
    .in0(in_2), .in1({not_3_out[31], not_4_out}), .out(multiplexer_2_out), .sel(in_2[31]));
  xor xor_1 (xor_1_out, in_1[31], in_2[31]);
  Multiplier #(.width(32)) multiplier_1 (
    .a(multiplexer_1_out), .b(multiplexer_2_out), .out(multiplier_1_out));  // open: cin, cout
  assign not_5_out = ~multiplier_1_out;  // NOT_Gate not_5, 32 bits wide
  Adder #(.width(32)) adder_1 (.a(not_5_out), .b(32'h1), .out(adder_1_out));  // open: cin, cout
  Multiplexer #(.width(32), .enable("false")) multiplexer_3 (
    .in0(multiplier_1_out), .in1(adder_1_out), .out(out_3), .sel(xor_1_out));
endmodule

module mulhu_6 (
  input  [31:0] in_1,
  input  [31:0] in_2,
  output [31:0] out_3
);

  Multiplier #(.width(32)) multiplier_1 (.a(in_1), .b(in_2), .cout(out_3));  // open: out, cin
endmodule

module mulh_7 (
  input  [31:0] in_1,
  input  [31:0] in_2,
  output [31:0] out_3
);

  wire adder_1_cout, xor_1_out;
  wire [30:0] not_2_out, not_4_out, subtractor_1_out, subtractor_2_out;
  wire [31:0] adder_2_out, bit_extender_1_out, multiplexer_1_out, multiplexer_2_out, multiplier_1_cout,
       multiplier_1_out, not_5_out, not_6_out;
  wire [31:31] not_1_out, not_3_out;

  Subtractor #(.width(31)) subtractor_1 (.a(in_1[30:0]), .b(31'h1), .out(subtractor_1_out));  // open: bin, bout
  Subtractor #(.width(31)) subtractor_2 (.a(in_2[30:0]), .b(31'h1), .out(subtractor_2_out));  // open: bin, bout
  not not_1 (not_1_out[31], in_1[31]);
  assign not_2_out = ~subtractor_1_out;  // NOT_Gate not_2, 31 bits wide
  not not_3 (not_3_out[31], in_2[31]);
  assign not_4_out = ~subtractor_2_out;  // NOT_Gate not_4, 31 bits wide
  Multiplexer #(.width(32), .enable("false")) multiplexer_1 (
    .in0(in_1), .in1({not_1_out[31], not_2_out}), .out(multiplexer_1_out), .sel(in_1[31]));
  Multiplexer #(.width(32), .enable("false")) multiplexer_2 (
    .in0(in_2), .in1({not_3_out[31], not_4_out}), .out(multiplexer_2_out), .sel(in_2[31]));
  xor xor_1 (xor_1_out, in_1[31], in_2[31]);
  Multiplier #(.width(32)) multiplier_1 (
    .a(multiplexer_1_out), .b(multiplexer_2_out), .out(multiplier_1_out), .cout(multiplier_1_cout));  // open: cin
  assign not_5_out = ~multiplier_1_out;  // NOT_Gate not_5, 32 bits wide
  assign not_6_out = ~multiplier_1_cout;  // NOT_Gate not_6, 32 bits wide
  Adder #(.width(32)) adder_1 (.a(not_5_out), .b(32'h1), .cout(adder_1_cout));  // open: out, cin
  assign bit_extender_1_out = {{31{1'b0}}, adder_1_cout};  // Bit_Extender bit_extender_1
  Adder #(.width(32)) adder_2 (.a(bit_extender_1_out), .b(not_6_out), .out(adder_2_out));  // open: cin, cout
  Multiplexer #(.width(32), .enable("false")) multiplexer_3 (
    .in0(multiplier_1_cout), .in1(adder_2_out), .out(out_3), .sel(xor_1_out));
endmodule

module divu_8 (
  input  [31:0] in_1,
  input  [31:0] in_2,
  output [31:0] out_3
);

  Divider #(.width(32)) divider_1 (.a(in_1), .b(in_2), .out(out_3));  // open: upper, rem
endmodule

module div_9 (
  input  [31:0] in_1,
  input  [31:0] in_2,
  output [31:0] out_3
);

  wire xor_1_out;
  wire [30:0] not_2_out, not_4_out, subtractor_1_out, subtractor_2_out;
  wire [31:0] adder_1_out, divider_1_out, multiplexer_1_out, multiplexer_2_out, not_5_out;
  wire [31:31] not_1_out, not_3_out;

  Subtractor #(.width(31)) subtractor_1 (.a(in_1[30:0]), .b(31'h1), .out(subtractor_1_out));  // open: bin, bout
  Subtractor #(.width(31)) subtractor_2 (.a(in_2[30:0]), .b(31'h1), .out(subtractor_2_out));  // open: bin, bout
  not not_1 (not_1_out[31], in_1[31]);
  assign not_2_out = ~subtractor_1_out;  // NOT_Gate not_2, 31 bits wide
  not not_3 (not_3_out[31], in_2[31]);
  assign not_4_out = ~subtractor_2_out;  // NOT_Gate not_4, 31 bits wide
  Multiplexer #(.width(32), .enable("false")) multiplexer_1 (
    .in0(in_1), .in1({not_1_out[31], not_2_out}), .out(multiplexer_1_out), .sel(in_1[31]));
  Multiplexer #(.width(32), .enable("false")) multiplexer_2 (
    .in0(in_2), .in1({not_3_out[31], not_4_out}), .out(multiplexer_2_out), .sel(in_2[31]));
  xor xor_1 (xor_1_out, in_1[31], in_2[31]);
  Divider #(.width(32)) divider_1 (
    .a(multiplexer_1_out), .b(multiplexer_2_out), .out(divider_1_out));  // open: upper, rem
  assign not_5_out = ~divider_1_out;  // NOT_Gate not_5, 32 bits wide
  Adder #(.width(32)) adder_1 (.a(not_5_out), .b(32'h1), .out(adder_1_out));  // open: cin, cout
  Multiplexer #(.width(32), .enable("false")) multiplexer_3 (
    .in0(divider_1_out), .in1(adder_1_out), .out(out_3), .sel(xor_1_out));
endmodule

module remu_10 (
  input  [31:0] in_1,
  input  [31:0] in_2,
  output [31:0] out_3
);

  Divider #(.width(32)) divider_1 (.a(in_1), .b(in_2), .rem(out_3));  // open: out, upper
endmodule

module srl_11 (
  input  [31:0] in_1,
  input  [31:0] in_2,
  output [31:0] out_3
);

  wire [4:0] bit_extender_1_out;

  Bit_Extender #(.in_width(32), .out_width(5)) bit_extender_1 (.in(in_2), .out(bit_extender_1_out));
  Shifter #(.width(32), .shift("lr")) shifter_1 (.in(in_1), .\dist (bit_extender_1_out), .out(out_3));
endmodule

module sra_12 (
  input  [31:0] in_1,
  input  [31:0] in_2,
  output [31:0] out_3
);

  wire [4:0] bit_extender_1_out;

  Bit_Extender #(.in_width(32), .out_width(5)) bit_extender_1 (.in(in_2), .out(bit_extender_1_out));
  Shifter #(.width(32), .shift("ar")) shifter_1 (.in(in_1), .\dist (bit_extender_1_out), .out(out_3));
endmodule

module slt_13 (
  input  [31:0] A,
  input  [31:0] B,
  output [31:0] out_3
);

  wire comparator_1_lt;

  Comparator #(.width(32)) comparator_1 (.a(A), .b(B), .lt(comparator_1_lt));  // open: gt, eq
  assign out_3 = {{31{1'b0}}, comparator_1_lt};  // Bit_Extender bit_extender_1
endmodule

module sir_14 (
  input  [31:0] A,
  input  [31:0] B,
  output [31:0] out_3
);

  wire comparator_1_eq;

  Comparator #(.width(32)) comparator_1 (
    .a({A[0], A[1], A[2], A[3], A[4], A[5], A[6], A[7], A[8], A[9], A[10], A[11], A[12], A[13], A[14], A[15], A[16], A[17], A[18], A[19], A[20], A[21], A[22], A[23], A[24], A[25], A[26], A[27], A[28], A[29], A[30], A[31]}),
    .b(B), .eq(comparator_1_eq));  // open: gt, lt
  assign out_3 = {{31{1'b0}}, comparator_1_eq};  // Bit_Extender bit_extender_1
endmodule

module cnto_15 (
  input  [31:0] in_1,
  input  [31:0] in_2,
  output [31:0] out_3
);

  wire [6:0] bitadder_1_out;

  BitAdder #(.width(32)) bitadder_1 (.in0(in_1), .in1(in_2), .out(bitadder_1_out));
  assign out_3 = {{25{bitadder_1_out[6]}}, bitadder_1_out};  // Bit_Extender bit_extender_1
endmodule
