// Logisim project regfile.circ as structural Verilog: 1 circuit, main circuit main
module main (
  input  ZREO,
  input  [4:0] rs1,
  input  [4:0] rs2,
  input  [4:0] rd,
  input  [31:0] Write_Data,
  input  RegWEn,
  input  clk,
  output [31:0] ra,
  output [31:0] sp,
  output [31:0] t0,
  output [31:0] t1,
  output [31:0] t2,
  output [31:0] s0,
  output [31:0] s1,
  output [31:0] a0,
  output [31:0] Read_Data_1,
  output [31:0] Read_Data_2
);

  wire multiplexer_1_out, multiplexer_2_out, multiplexer_3_out, multiplexer_4_out, multiplexer_5_out,
       multiplexer_6_out, multiplexer_7_out, multiplexer_8_out, WE1, WE2, WE5, WE6, WE7, WE8, WE9, WE10;
  wire [31:0] Input_x1, Input_x2, Input_x5, Input_x6, Input_x7, Input_x8, Input_x9, Input_x10, output_x0;

  Register #(.width(32)) x0 (.D({32{1'b0}}), .en(ZREO), .clk(clk), .Q(output_x0));  // open: clr
  Register #(.width(32)) x1 (.D(Input_x1), .en(multiplexer_1_out), .clk(clk), .Q(ra));  // open: clr
  Multiplexer #(.enable("false")) multiplexer_1 (.in0(1'b0), .in1(RegWEn), .out(multiplexer_1_out), .sel(WE1));
  Register #(.width(32)) x2 (.D(Input_x2), .en(multiplexer_2_out), .clk(clk), .Q(sp));  // open: clr
  Multiplexer #(.enable("false")) multiplexer_2 (.in0(1'b0), .in1(RegWEn), .out(multiplexer_2_out), .sel(WE2));
  Multiplexer #(.enable("false")) multiplexer_3 (.in0(1'b0), .in1(RegWEn), .out(multiplexer_3_out), .sel(WE6));
  Multiplexer #(.enable("false")) multiplexer_4 (.in0(1'b0), .in1(RegWEn), .out(multiplexer_4_out), .sel(WE7));
  Register #(.width(32)) x5 (.D(Input_x5), .en(multiplexer_5_out), .clk(clk), .Q(t0));  // open: clr
  Multiplexer #(.enable("false")) multiplexer_5 (.in0(1'b0), .in1(RegWEn), .out(multiplexer_5_out), .sel(WE5));
  Register #(.width(32)) x6 (.D(Input_x6), .en(multiplexer_3_out), .clk(clk), .Q(t1));  // open: clr
  Register #(.width(32)) x7 (.D(Input_x7), .en(multiplexer_4_out), .clk(clk), .Q(t2));  // open: clr
  Multiplexer #(.enable("false")) multiplexer_6 (.in0(1'b0), .in1(RegWEn), .out(multiplexer_6_out), .sel(WE8));
  Multiplexer #(.enable("false")) multiplexer_7 (.in0(1'b0), .in1(RegWEn), .out(multiplexer_7_out), .sel(WE9));
  Multiplexer #(.enable("false")) multiplexer_8 (.in0(1'b0), .in1(RegWEn), .out(multiplexer_8_out), .sel(WE10));
  Register #(.width(32)) x8 (.D(Input_x8), .en(multiplexer_6_out), .clk(clk), .Q(s0));  // open: clr
  Register #(.width(32)) x9 (.D(Input_x9), .en(multiplexer_7_out), .clk(clk), .Q(s1));  // open: clr
  Register #(.width(32)) x10 (.D(Input_x10), .en(multiplexer_8_out), .clk(clk), .Q(a0));  // open: clr
  Multiplexer #(.select(5), .width(32), .enable("false")) multiplexer_9 (
    .in0(output_x0), .in1(ra), .in2(sp), .in5(t0), .in6(t1), .in7(t2), .in8(s0), .in9(s1), .in10(a0),
    .out(Read_Data_1), .sel(rs1));  // open: in3, in4, in11, in12, in13, in14, in15, in16, in17, in18, in19, in20, in21, in22, in23, in24, in25, in26, in27, in28, in29, in30, in31
  Demultiplexer #(.select(5), .width(32), .enable("false")) demultiplexer_1 (
    .out1(Input_x1), .out2(Input_x2), .out5(Input_x5), .out6(Input_x6), .out7(Input_x7), .out8(Input_x8),
    .out9(Input_x9), .out10(Input_x10), .in(Write_Data), .sel(rd));  // open: out0, out3, out4, out11, out12, out13, out14, out15, out16, out17, out18, out19, out20, out21, out22, out23, out24, out25, out26, out27, out28, out29, out30, out31
  Multiplexer #(.select(5), .width(32), .enable("false")) multiplexer_10 (
    .in0(output_x0), .in1(ra), .in2(sp), .in5(t0), .in6(t1), .in7(t2), .in8(s0), .in9(s1), .in10(a0),
    .out(Read_Data_2), .sel(rs2));  // open: in3, in4, in11, in12, in13, in14, in15, in16, in17, in18, in19, in20, in21, in22, in23, in24, in25, in26, in27, in28, in29, in30, in31
  Demultiplexer #(.select(5), .enable("false")) demultiplexer_2 (
    .out1(WE1), .out2(WE2), .out5(WE5), .out6(WE6), .out7(WE7), .out8(WE8), .out9(WE9), .out10(WE10),
    .in(RegWEn), .sel(rd));  // open: out0, out3, out4, out11, out12, out13, out14, out15, out16, out17, out18, out19, out20, out21, out22, out23, out24, out25, out26, out27, out28, out29, out30, out31

  // Other names for the same wires on the sheet: output_x1[31:0] = ra; output_x2[31:0] = sp; output_x5[31:0] = t0;
  //   output_x6[31:0] = t1; output_x7[31:0] = t2; output_x8[31:0] = s0; output_x9[31:0] = s1; output_x10[31:0] = a0;
  //   read_data1[31:0] = Read_Data_1; read_data2[31:0] = Read_Data_2; read_reg1[4:0] = rs1; read_reg2[4:0] = rs2;
  //   write_en = RegWEn; write_en_off = ZREO; write_reg[4:0] = rd

  // Notes on the sheet:
  //   INPUTS to your circuit
  //   DON'T CHANGE THE LOCATIONS OF THE INPUTS AND OUTPUTS!
  //   These are DEBUG/TEST outputs from your circuit.
  //   OUTPUTS from your circuit
endmodule
